# Fritzing sketch tesi (saved by Fritzing 0.9.3b)
breadboards: 2

parts:
  Componente1 = Arduino Mega 2560 (Rev3)
  R1 = Resistor [tolerance=±5% resistance=220 package=THT]
  R2 = Resistor [tolerance=±5% resistance=220 package=THT]
  R3 = Photocell (LDR) [package=THT]
  R4 = Photocell (LDR) [package=THT]
  e-radionica1 = TCS230 Color Sensor [part_number=101209]
  hc-sr1 = hc-sr04
  hc-sr2 = hc-sr04
  J1 = Basic Servo
  VCC1 = Battery
  VCC2 = Battery
  J2 = Basic Servo
  J3 = Basic Servo
  M1 = DC Motor

nets:
  N1: Componente1.A2, R1.Pin_1, R4.pin_0
  N2: Componente1.A3, R2.Pin_1, R3.pin_0
  N3: Componente1.D12_PWM, hc-sr2.Trig
  N4: Componente1.D11_PWM, hc-sr2.Echo
  N5: Componente1.D10_PWM, hc-sr1.Trig
  N6: Componente1.D9_PWM, hc-sr1.Echo
  N7: Componente1.D8_PWM, e-radionica1.OE
  5V: Componente1.5V, R3.pin_1, R4.pin_1, e-radionica1.Vcc
  GND: Componente1.GND, R1.Pin_0, R2.Pin_0, e-radionica1.Gnd
  N8: Componente1.D1_TX0, J3.pulse
  N9: Componente1.D2_PWM, J2.pulse
  N10: Componente1.D3_PWM, e-radionica1.S0
  N11: Componente1.D4_PWM, e-radionica1.S1
  N12: Componente1.D5_PWM, e-radionica1.S3
  N13: Componente1.D6_PWM, e-radionica1.S2
  N14: Componente1.D7_PWM, e-radionica1.Out
  N15: Componente1.D52, J1.pulse
  VCC: hc-sr1.VCC, hc-sr2.VCC
  GND_2: hc-sr1.GND, hc-sr2.GND
  GND_3: J1.gnd, VCC1.-, VCC2.-, J2.gnd, J3.gnd
  VCC_2: J1.vcc, VCC1.+, VCC2.+, J2.vcc, J3.vcc, M1.pin_1, M1.pin_2

custom parts:
  TCS230 Color Sensor: TCS230

// code stored in the sketch: tesi.ino
#include <NewPing.h>
#include <Servo.h>
#include "HX711.h"

// HX711.DOUT  - pin #A4
// HX711.PD_SCK - pin #A5

HX711 scale(A4, A5);    // parameter "gain" is ommited; the default value 128 is used by the library



NewPing sonar1(10, 9, 200);
NewPing sonar2(12, 11, 200);
int magnetic, md,  luce1, luce2, distanza1 ;
const int s0 = 3;  
const int s1 = 4;  
const int s2 =7;  
const int s3 = 5;  
const int out = 6; 
const int motorpin = 52;
Servo motoreservo;   
int frequency = 0;
int color=0;

void setup() {
  // put your setup code here, to run once:
  
  pinMode(A2,INPUT);
  pinMode(A3,INPUT);
  pinMode(A0,INPUT);
  
  Serial.begin(9600);

  pinMode(s0, OUTPUT);  
  pinMode(s1, OUTPUT);  
  pinMode(s2, OUTPUT);  
  pinMode(s3, OUTPUT);  
  pinMode(out, INPUT);   
  motoreservo.attach(motorpin);
  digitalWrite(s0, HIGH);  
  digitalWrite(s1, LOW); 



  // set HX711
  scale.set_scale(2280.f);                    
  scale.tare();              
}

void loop() {
  // put your main code here, to run repeatedly:



    
    magnetic=analogRead(A0);
    luce1=analogRead(A2);
    luce2=analogRead(A3);
    unsigned int distanza1 = sonar1.ping();
    distanza1=distanza1 / US_ROUNDTRIP_CM;
    
    unsigned int distanza2 = sonar2.ping();
    distanza2=distanza2 / US_ROUNDTRIP_CM;
 
    Serial.print(luce1);
    Serial.print(",");
    Serial.print(luce2);
    Serial.print(",");
    Serial.print(distanza1);
    Serial.print(",");
    Serial.print(distanza2);
    Serial.print(",");
    color = readColor();
    Serial.print(scale.get_units(10)*28.3495231, 1);
    Serial.println("");
    


  
    color=0;
    scale.power_down();          
    delay(5000);
    scale.power_up();


    char a;
    a = Serial.read ();
    switch (a) {
      case '1': // tira su
        motoreservo.write(80);
        Serial.println("SU");
        break;
      case '2': // tira giu
        motoreservo.write(15);
        Serial.println("GIU");
        break;
      case '3': // Ricalcola
        motoreservo.write(60);
        delay(1000);
        motoreservo.write(70);
        Serial.println("Ricalcola");
        break;
      default : // In tutti gli altri casi visualizzo un messaggio
        
        break;
    }

    
}




//Read-Color Function
int readColor() {
  
  //Setting red filtered photodiodes to be read
  digitalWrite(s2, LOW);
  digitalWrite(s3, LOW);
  
  //Reading the output frequency
  frequency = pulseIn(out, LOW);
  int R = frequency;
  
  //Printing the value on the serial monitor
  Serial.print(frequency);  //printing rosso color frequency
  Serial.print(",");
  
  
  //Setting Green filtered photodiodes to be read
  digitalWrite(s2, HIGH);
  digitalWrite(s3, HIGH);
  
  //Reading the output frequency
  frequency = pulseIn(out, LOW);
  int G = frequency;
  
  //Printing the value on the serial monitor
  Serial.print(frequency);  //printing verde color frequency
  Serial.print(",");
  
  
  //Setting Blue filtered photodiodes to be read
  digitalWrite(s2, LOW);
  digitalWrite(s3, HIGH);
  
  //Reading the output frequency
  frequency = pulseIn(out, LOW);
  int B = frequency;
  
  //Printing the value on the serial monitor
  Serial.print(frequency);  //printing blu color frequency
  Serial.print(",");
  
  
  
  if(R<260 & R>230 & G<860 & G>800){
    color = 1; // Red
  }
  if(G<420 & G>370 & B<350 & B>305){
    color = 2; // Blue
  }
  if(R<450 & R>420 & G<420 & G>390){
    color = 3; // Green
  }
  return color;  
}
